# Fritzing sketch DS18B20 (saved by Fritzing 0.8.7b)

parts:
  Part1 = Arduino Pro Mini v13
  DS4 = DS18B20 1-Wire Temperature Sensor Probe Cable  # not connected
  DS5 = DS18B20 1-Wire Temperature Sensor Probe Cable
  R1 = Resistor [tolerance=±5% resistance=4.7k package=THT]

nets:
  GND: Part1.GND, DS5.GND
  VCC: Part1.VCC, DS5.VDD, R1.Pin_1
  N1: Part1.D3_PWM, DS5.DQ, R1.Pin_0
