# Fritzing sketch Senior Design (saved by Fritzing 0.8.7b)
breadboards: 2

parts:
  Part1 = Arduino Pro Mini v13
  DS1 = DS18B20 1-Wire Temperature Sensor [part_number=DS18B20]  # not connected
  DS2 = DS18B20 1-Wire Temperature Sensor Probe Cable  # not connected
  U1 = XBEE-1 [package=xbee-1_lock]  # not connected
  U2 = XBEE-1 [package=xbee-1_lock]  # not connected
  Part2 = Adafruit DS3231 [part_number="Adafruit #3013"]  # not connected
  Part3 = Adafruit TSL2561 [part_number="Adafruit #439"]  # not connected
  Part4 = MicroSD Card Module  # not connected
  DS3 = DS18B20 1-Wire Temperature Sensor Probe Cable  # not connected
  ZS-042_RTC1 = ZS-042 RTC Module  # not connected
  Part5 = FTDI Basic Programmer  # not connected

nets:
  N1: Part1.DTR, Part1.D0/TX, Part1.D1/RX

custom parts:
  Adafruit DS3231: The datasheet for the DS3231 explains that this part is an "Extremely Accurate I²C-Integrated RTC/TCXO/Crystal". And, hey, it does exactly what it says on the tin! This Real Time Clock (RTC) is the most precise you can get in a small, low power package. Most RTCs use an external 32kHz timing crystal that is used to keep time with low current draw. And that's all well and good, but those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
  Adafruit TSL2561: The TSL2561 luminosity sensor is an advanced digital light sensor, ideal for use in a wide range of light situations. Compared to low cost CdS cells, this sensor is more precise, allowing for exact lux calculations and can be configured for different gain/timing ranges to detect light ranges from up to 0.1 - 40,000+ Lux on the fly. The best part of this sensor is that it contains both infrared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
